// Logisim project rl_cpu.circ as structural Verilog: 1 circuit, main circuit main
module main (
  input  [2:0] in_1,
  input  in_2,
  input  in_3,
  input  in_4,
  output [15:0] BUS_status,
  output [15:0] out_6
);

  wire _012345678901234567890123456789012_q0, _012345678901234567890123456789012_q1,
       _012345678901234567890123456789012_q2, _012345678901234567890123456789012_q5,
       _012345678901234567890123456789012_q6, _012345678901234567890123456789012_q7,
       _012345678901234567890123456789012_q8, _012345678901234567890123456789012_q9,
       _012345678901234567890123456789012_q12, _012345678901234567890123456789012_q14,
       _012345678901234567890123456789012_q15, _012345678901234567890123456789012_q16,
       _012345678901234567890123456789012_q17, _012345678901234567890123456789012_q18,
       _012345678901234567890123456789012_q21, ALE, ALUMUX, and_1_out, and_2_out, and_4_out, and_5_out,
       and_6_out, and_7_out, and_8_out, and_9_out, and_10_out, and_11_out, and_12_out, and_13_out,
       and_14_out, and_17_out, and_18_out, and_19_out, and_20_out, and_21_out, BPE, button_1_out,
       button_3_out, button_4_out, d_ff_2_q, DC_Clk, DCDL, decoder_1_out0, decoder_1_out1, decoder_1_out2,
       decoder_2_out2, decoder_2_out3, decoder_3_out0, decoder_3_out1, decoder_3_out2, decoder_3_out3,
       decoder_3_out4, decoder_3_out5, decoder_3_out6, decoder_3_out7, demultiplexer_1_out1,
       demultiplexer_2_out0, demultiplexer_3_out0, demultiplexer_3_out1, demultiplexer_4_out1,
       demultiplexer_4_out2, demultiplexer_4_out3, Goto_state_0_out, ILE, IntProcess, IntProcessEnd,
       IntProcessStart, IntVectorMux, IRQ, JMP_BIT, JMP_OK, LFRC_Out, LFRC_Reset, LFRC_Set, LoadFromPc,
       LoadFromResPc, MainClock, nand_1_out, nor_1_out, not_1_out, not_2_out, not_3_out, not_4_out,
       not_5_out, not_6_out, not_7_out, not_8_out, not_9_out, not_10_out, or_1_out, P0E, PcClock, PcIntClock,
       PcLoad, PcMux, RAE, RamClock, RamCS, RBE, RCE, RCMux, READ_WR, RSI, TTYClock_out;
  wire [1:0] DC_q, Instruction_Latch_q_2, Instruction_Latch_q_3, Instruction_Latch_q_4, multiplexer_4_out,
       or_11_out, RS_q;
  wire [2:0] and_15_out, comparator_1_eq, Instruction_Latch_q_5;
  wire [6:0] keyboard_1_data;
  wire [15:0] adder_1_out, adder_2_out, Address_Latch_q, and_16_out, BASE_POINTER_q, controlled_buffer_1_out,
       or_13_out, PC_Int_Latch_q, PC_q, PORT_0_q, PORT_1_q, PORT_2_q, RA_q, ram_3_data, RB_q, RC_q,
       subtractor_1_out;
  wire [15:12] Instruction_Latch_q;

  D_Flip_Flop u_IRQ (.Q(IRQ), .preset(and_1_out), .reset(IntProcessStart));  // open: clk, D, Qn, en
  and and_1 (and_1_out, in_4, not_1_out);
  not not_1 (not_1_out, IntProcess);
  Multiplexer #(.width(16)) multiplexer_1 (.in0(16'h20), .out(BUS_status), .sel(1'b0), .en(IntVectorMux));  // open: in1
  Register #(.width(16)) PC_Int_Latch (.D(BUS_status), .en(1'b1), .Q(PC_Int_Latch_q), .clk(PcIntClock));  // open: clr
  Multiplexer #(.width(16)) multiplexer_2 (
    .in0(PC_Int_Latch_q), .out(BUS_status), .sel(1'b0), .en(IntProcessEnd));  // open: in1
  D_Flip_Flop u_IntProcess (.Q(IntProcess), .preset(IntProcessStart), .reset(IntProcessEnd));  // open: clk, D, Qn, en
  not not_2 (not_2_out, Instruction_Latch_q[15]);
  Button button_1 (.out(button_1_out));
  Clock clock_1 (.out(MainClock));
  and and_2 (and_2_out, not_2_out, MainClock);
  not not_3 (not_3_out, PcLoad);
  or or_1 (or_1_out, _012345678901234567890123456789012_q12, and_8_out, Goto_state_0_out, and_4_out, and_9_out, and_7_out);
  not not_4 (not_4_out, or_1_out);
  Shift_Register #(.length(32)) _012345678901234567890123456789012 (
    .shift(not_4_out), .in(1'b0), .clk(and_2_out), .load(or_1_out), .d0(Goto_state_0_out),
    .q0(_012345678901234567890123456789012_q0), .d1(1'b0), .q1(_012345678901234567890123456789012_q1),
    .d2(1'b0), .q2(_012345678901234567890123456789012_q2), .d3(1'b0), .q3(ILE), .d4(and_9_out),
    .q4(LFRC_Reset), .d5(1'b0), .q5(_012345678901234567890123456789012_q5),
    .d6(_012345678901234567890123456789012_q12), .q6(_012345678901234567890123456789012_q6), .d7(1'b0),
    .q7(_012345678901234567890123456789012_q7), .d8(1'b0), .q8(_012345678901234567890123456789012_q8),
    .d9(1'b0), .q9(_012345678901234567890123456789012_q9), .d10(1'b0), .q10(LFRC_Set), .d11(1'b0),
    .q11(DCDL), .d12(1'b0), .q12(_012345678901234567890123456789012_q12), .d13(and_7_out), .q13(RSI),
    .d14(1'b0), .q14(_012345678901234567890123456789012_q14), .d15(1'b0),
    .q15(_012345678901234567890123456789012_q15), .d16(1'b0), .q16(_012345678901234567890123456789012_q16),
    .d17(and_8_out), .q17(_012345678901234567890123456789012_q17), .d18(1'b0),
    .q18(_012345678901234567890123456789012_q18), .d19(and_4_out), .q19(IntProcessStart), .d20(1'b0),
    .q20(IntVectorMux), .d21(1'b0), .q21(_012345678901234567890123456789012_q21), .d22(1'b0), .d23(1'b0),
    .d24(1'b0), .d25(1'b0), .d26(1'b0), .d27(1'b0), .d28(1'b0), .d29(1'b0), .d30(1'b0), .d31(1'b0));  // open: out, clr, q22, q23, q24, q25, q26, q27, q28, q29, q30, q31
  Counter #(.width(16), .max('hffff)) PC (
    .load(PcLoad), .D(BUS_status), .count(not_3_out), .Q(PC_q), .clk(PcClock), .clr(in_3));  // open: carry
  D_Flip_Flop d_ff_1 (.Q(LFRC_Out), .preset(LFRC_Set), .en(1'b1), .reset(LFRC_Reset));  // open: clk, D, Qn
  Multiplexer #(.width(16)) multiplexer_3 (.in0(PC_q), .out(BUS_status), .sel(1'b0), .en(PcMux));  // open: in1
  Button button_2 (.out(RamClock));
  D_Flip_Flop d_ff_2 (
    .clk(_012345678901234567890123456789012_q0), .D(1'b1), .Q(d_ff_2_q));  // open: Qn, preset, en, reset
  Demultiplexer demultiplexer_1 (
    .out0(ALUMUX), .out1(demultiplexer_1_out1), .in(_012345678901234567890123456789012_q18),
    .sel(LoadFromPc), .en(1'b1));
  not not_5 (not_5_out, d_ff_2_q);
  or Goto_state_0 (Goto_state_0_out, not_5_out, _012345678901234567890123456789012_q21, _012345678901234567890123456789012_q18, _012345678901234567890123456789012_q16);
  or or_2 (ALE, _012345678901234567890123456789012_q8, _012345678901234567890123456789012_q17, _012345678901234567890123456789012_q1);
  and and_3 (PcIntClock, _012345678901234567890123456789012_q1, not_6_out);
  not not_6 (not_6_out, IntProcess);
  or or_3 (RamCS, _012345678901234567890123456789012_q2, _012345678901234567890123456789012_q18, _012345678901234567890123456789012_q9);
  or or_4 (READ_WR, _012345678901234567890123456789012_q2, _012345678901234567890123456789012_q9);
  or or_5 (PcClock, _012345678901234567890123456789012_q21, LFRC_Reset, _012345678901234567890123456789012_q17, _012345678901234567890123456789012_q16);
  or or_6 (DC_Clk, _012345678901234567890123456789012_q5, DCDL);
  and and_4 (and_4_out, IRQ, _012345678901234567890123456789012_q1);
  not not_7 (not_7_out, JMP_BIT);
  and and_5 (and_5_out, JMP_BIT, JMP_OK, _012345678901234567890123456789012_q15);
  and and_6 (and_6_out, _012345678901234567890123456789012_q16, JMP_BIT, JMP_OK);
  Register #(.width(16)) Instruction_Latch (
    .D(BUS_status),
    .Q({Instruction_Latch_q, LoadFromResPc, Instruction_Latch_q_4, Instruction_Latch_q_3, Instruction_Latch_q_2, LoadFromPc, JMP_BIT, Instruction_Latch_q_5[0], Instruction_Latch_q_5[1], Instruction_Latch_q_5[2]}),
    .clk(ILE), .clr(button_3_out));  // open: en
  Button button_3 (.out(button_3_out));
  and and_7 (and_7_out, _012345678901234567890123456789012_q6, nor_1_out);
  and and_8 (and_8_out, _012345678901234567890123456789012_q15, not_7_out);
  or or_7 (PcLoad, and_5_out, _012345678901234567890123456789012_q21, IntVectorMux, and_6_out);
  Multiplexer #(.select(2), .width(2)) multiplexer_4 (
    .in0(Instruction_Latch_q_2), .in1(Instruction_Latch_q_3), .in2(Instruction_Latch_q_4),
    .out(multiplexer_4_out), .sel(RS_q), .en(1'b1));  // open: in3
  Counter #(.width(2), .max('h3)) RS (.count(1'b1), .Q(RS_q), .clk(RSI), .clr(ILE));  // open: load, D, carry
  and and_9 (and_9_out, _012345678901234567890123456789012_q14, nand_1_out);
  or or_8 (RCMux, demultiplexer_2_out0, and_10_out);
  Demultiplexer demultiplexer_2 (
    .out0(demultiplexer_2_out0), .out1(IntProcessEnd), .in(_012345678901234567890123456789012_q15),
    .sel(LoadFromResPc), .en(1'b1));
  Decoder #(.select(2)) decoder_1 (
    .out0(decoder_1_out0), .out1(decoder_1_out1), .out2(decoder_1_out2), .sel(RS_q));  // open: out3, en
  Counter #(.width(2), .max('h3)) DC (
    .load(1'b1), .D(multiplexer_4_out), .count(DCDL), .Q(DC_q), .clk(DC_Clk));  // open: carry, clr
  nor nor_1 (nor_1_out, DC_q[1], DC_q[0]);
  nand nand_1 (nand_1_out, RS_q[0], RS_q[1]);
  and and_10 (and_10_out, _012345678901234567890123456789012_q7, LFRC_Out);
  Register #(.width(16)) BASE_POINTER (.Q(BASE_POINTER_q));  // open: D, en, clk, clr
  // NAND_Gate nand_2 has open pins: in0=DC_q[0], in1=DC_q[1], out=open
  and and_11 (and_11_out, _012345678901234567890123456789012_q7, not_8_out);
  not not_8 (not_8_out, LFRC_Out);
  assign controlled_buffer_1_out = BPE ? BASE_POINTER_q : 16'bz;  // Controlled_Buffer controlled_buffer_1
  Pull_Resistor pull_resistor_1 (.node(controlled_buffer_1_out));
  Register #(.width(16)) RC (.D(BUS_status), .Q(RC_q), .clk(RCE));  // open: en, clr
  and and_12 (and_12_out, Instruction_Latch_q[12], decoder_1_out0);
  or or_9 (BPE, and_12_out, and_13_out, and_14_out);
  and and_13 (and_13_out, Instruction_Latch_q[13], decoder_1_out1);
  and and_14 (and_14_out, Instruction_Latch_q[14], decoder_1_out2);
  or or_10 (PcMux, _012345678901234567890123456789012_q0, demultiplexer_1_out1, and_11_out);
  Adder #(.width(16)) adder_1 (.a(controlled_buffer_1_out), .b(RC_q), .out(adder_1_out));  // open: cin, cout
  Register #(.width(16)) RA (.D(BUS_status), .Q(RA_q), .clk(RAE));  // open: en, clr
  Register #(.width(16)) RB (.D(BUS_status), .Q(RB_q), .clk(RBE));  // open: en, clr
  or or_11 (or_11_out[0], DC_q[1], RS_q[0]);
  or or_12 (or_11_out[1], RS_q[1], DC_q[1]);
  Multiplexer #(.width(16)) multiplexer_5 (.in0(adder_1_out), .out(BUS_status), .sel(1'b0), .en(RCMux));  // open: in1
  assign and_15_out = Instruction_Latch_q_5 & comparator_1_eq;  // AND_Gate and_15, 3 bits wide
  nor nor_2 (JMP_OK, and_15_out[2], and_15_out[1], and_15_out[0]);
  Decoder #(.select(2)) decoder_2 (
    .out0(RAE), .out1(RBE), .out2(decoder_2_out2), .out3(decoder_2_out3), .sel(or_11_out), .en(LFRC_Set));
  Adder #(.width(16)) adder_2 (.a(RA_q), .b(RB_q), .out(adder_2_out));  // open: cin, cout
  Subtractor #(.width(16)) subtractor_1 (.a(RA_q), .b(RB_q), .out(subtractor_1_out));  // open: bin, bout
  assign and_16_out = RA_q & RB_q;  // AND_Gate and_16, 16 bits wide
  assign or_13_out = RA_q | RB_q;  // OR_Gate or_13, 16 bits wide
  Comparator #(.width(16)) comparator_1 (
    .a(RA_q), .b(RB_q), .gt(comparator_1_eq[2]), .eq(comparator_1_eq[0]), .lt(comparator_1_eq[1]));
  Pull_Resistor pull_resistor_2 (.node(decoder_2_out2));
  Pull_Resistor pull_resistor_3 (.node(decoder_2_out3));
  Pull_Resistor pull_resistor_4 (.node(RAE));
  Pull_Resistor pull_resistor_5 (.node(RBE));
  or or_14 (RCE, decoder_2_out2, decoder_2_out3);
  Pull_Resistor pull_resistor_6 (.node(RCE));
  Multiplexer #(.select(3), .width(16)) multiplexer_6 (
    .in0({RA_q[14:0], 1'b0}), .in1({1'b0, RA_q[15:1]}), .in2(adder_2_out), .in3(subtractor_1_out),
    .in4(and_16_out), .in5(or_13_out), .out(BUS_status),
    .sel({Instruction_Latch_q_5[0], Instruction_Latch_q_5[1], Instruction_Latch_q_5[2]}), .en(ALUMUX));  // open: in6, in7
  Register #(.width(16)) Address_Latch (.D(BUS_status), .Q(Address_Latch_q), .clk(ALE));  // open: en, clr
  Decoder #(.select(3)) decoder_3 (
    .out0(decoder_3_out0), .out1(decoder_3_out1), .out2(decoder_3_out2), .out3(decoder_3_out3),
    .out4(decoder_3_out4), .out5(decoder_3_out5), .out6(decoder_3_out6), .out7(decoder_3_out7),
    .sel(Address_Latch_q[15:13]), .en(1'b1));
  and and_17 (and_17_out, RamCS, decoder_3_out1);
  Demultiplexer #(.select(3)) demultiplexer_3 (
    .out0(demultiplexer_3_out0), .out1(demultiplexer_3_out1), .in(and_17_out), .sel(Address_Latch_q[2:0]));  // open: out2, out3, out4, out5, out6, out7, en
  RAM #(.addrWidth(13), .dataWidth(16), .bus("asynch")) ram_1 ();  // open: addr, data, sel, ld, clr
  // OR_Gate or_15 has open pins: in0=decoder_3_out2, in1=decoder_3_out3, out=open
  // OR_Gate or_16 has open pins: in0=decoder_3_out4, in1=decoder_3_out5, in2=decoder_3_out6, in3=decoder_3_out7, out=open
  not not_9 (not_9_out, and_19_out);
  Register #(.width(16), .trigger("high")) PORT_0 (
    .D(BUS_status), .en(demultiplexer_3_out0), .Q(PORT_0_q), .clk(MainClock), .clr(TTYClock_out));
  Clock #(.highDuration(2), .lowDuration(2)) TTYClock (.out(TTYClock_out));
  not not_10 (not_10_out, demultiplexer_3_out1);
  Keyboard keyboard_1 (.clk(not_10_out), .clr(button_4_out), .data(keyboard_1_data));  // open: re, avail
  Button button_4 (.out(button_4_out));
  and and_18 (and_18_out, decoder_3_out0, RamCS);
  and and_19 (and_19_out, out_6[15], out_6[14], out_6[13], out_6[12], out_6[11], out_6[10], out_6[9], out_6[8], out_6[7], out_6[6], out_6[5], out_6[4], out_6[3], out_6[2]);
  Register #(.width(16)) Address_Latch_2 (.D(ram_3_data), .Q(out_6), .clk(ALE));  // open: en, clr
  TTY tty_1 (.data(PORT_0_q[6:0]), .clk(TTYClock_out));  // open: we, clr
  assign BUS_status = demultiplexer_3_out1 ? {{9{1'b0}}, keyboard_1_data} : 16'bz;  // Controlled_Buffer controlled_buffer_2
  RAM #(.addrWidth(13), .dataWidth(16), .bus("asynch")) ram_2 (
    .addr(Address_Latch_q[12:0]), .data(BUS_status), .sel(and_18_out), .ld(READ_WR));  // open: clr
  and and_20 (and_20_out, and_19_out, RamCS);
  Demultiplexer #(.select(2)) demultiplexer_4 (
    .out0(P0E), .out1(demultiplexer_4_out1), .out2(demultiplexer_4_out2), .out3(demultiplexer_4_out3),
    .in(and_20_out), .sel(out_6[1:0]));  // open: en
  and and_21 (and_21_out, not_9_out, 1'b0);
  RAM #(.addrWidth(16), .dataWidth(16), .bus("asynch")) ram_3 (
    .addr(out_6), .data(ram_3_data), .sel(and_21_out), .ld(READ_WR));  // open: clr
  Register #(.width(16), .trigger("high")) PORT_1 (
    .D(ram_3_data), .en(demultiplexer_4_out1), .Q(PORT_1_q), .clk(MainClock));  // open: clr
  Register #(.width(16), .trigger("high")) PORT_2 (
    .D(ram_3_data), .en(demultiplexer_4_out2), .Q(PORT_2_q), .clk(MainClock));  // open: clr
  Hex_Digit_Display hex_digit_display_1 (.value(PORT_2_q[15:12]));  // open: dp
  Hex_Digit_Display hex_digit_display_2 (.value(PORT_1_q[15:12]));  // open: dp
  Hex_Digit_Display hex_digit_display_3 (.value(PORT_1_q[11:8]));  // open: dp
  Hex_Digit_Display hex_digit_display_4 (.value(PORT_2_q[7:4]));  // open: dp
  Hex_Digit_Display hex_digit_display_5 (.value(PORT_2_q[11:8]));  // open: dp
  Hex_Digit_Display hex_digit_display_6 (.value(PORT_1_q[3:0]));  // open: dp
  Hex_Digit_Display hex_digit_display_7 (.value(PORT_1_q[7:4]));  // open: dp
  Hex_Digit_Display hex_digit_display_8 (.value(PORT_2_q[3:0]));  // open: dp

  // Other names for the same wires on the sheet: ALUOP[2:0] = in_1; ManualInput = in_2; PcIntMux = IntProcessEnd;
  //   PcReset = in_3; RDE = LFRC_Set; RSR = ILE

  // Notes on the sheet:
  //   ROM
endmodule
