// Logisim project cpu_bp.circ as structural Verilog: 1 circuit, main circuit main
module main (
  input  in_1,
  input  in_2,
  input  in_3,
  input  IRQ,
  input  in_5,
  input  in_6,
  input  in_7,
  input  in_8,
  input  [15:0] in_9,
  input  in_10,
  input  in_11,
  input  in_12,
  input  in_13,
  input  in_14,
  input  in_15,
  input  in_16,
  input  in_17,
  input  in_18,
  input  in_19,
  input  in_20,
  input  in_21,
  input  in_22,
  input  in_23,
  input  in_24,
  input  in_25,
  input  in_26,
  input  in_27,
  input  in_28,
  input  in_29,
  input  in_30,
  input  in_31,
  input  in_32,
  input  in_33,
  output [15:0] out_34
);

  wire AccessCode, ALUOE, and_1_out, and_7_out, clock_1_out, clock_2_out, controlled_buffer_1_out,
       controlled_buffer_34_out, controlled_buffer_35_out, decoder_1_out0, decoder_1_out1, decoder_1_out3,
       decoder_2_out0, decoder_2_out1, decoder_2_out2, decoder_2_out3, decoder_4_out0, decoder_4_out1,
       decoder_4_out2, decoder_4_out3, decoder_5_out0, decoder_5_out2, decoder_5_out3, decoder_6_out0,
       decoder_6_out1, decoder_6_out2, decoder_6_out3, decoder_6_out4, decoder_6_out5, Interrupt, IntOE,
       IntReset, InvClock, IRClk, JumpAccepted, MainClock, MCRST, ML, MR, MW, MWProtected, not_1_out,
       not_2_out, not_3_out, not_4_out, not_5_out, or_1_out, or_2_out, or_6_out, or_7_out, or_8_out,
       or_9_out, or_10_out, OverlapClock, PCCondLoad, PCLatchClk, PCLatchOE, PCLoad, PCOE, PCUp, PCV0, PCV1,
       RAClk, RBClk, RCClk, RCOE, SPDown, SPLoad, SPOE, SPUp, UserMode_q, UserReset, UserSet;
  wire [1:0] counter_1_q, RB_q;
  wire [1:1] RA_q_2;
  wire [2:0] and_6_out, comparator_1_gt;
  wire [3:0] ALUOp;
  wire [4:0] mCodeAL_q, SeqCntr_q;
  wire [6:0] controlled_buffer_9_out;
  wire [7:0] and_3_out, and_4_out, pull_resistor_1_node, pull_resistor_2_node, rom_1_data, rom_2_data,
       rom_3_data;
  wire [7:2] controlled_buffer_37_out, controlled_buffer_39_out, undriven, undriven_2;
  wire [13:0] PC_q, PCLatch_q, RB_q_2;
  wire [14:0] RA_q;
  wire [15:0] adder_1_out, adder_2_out, adder_3_out, AddrBUS, and_5_out, BP_2_q, BP_q, buffer_1_out,
       controlled_buffer_5_out, controlled_buffer_40_out, controlled_buffer_47_out, controlled_buffer_49_out,
       MainBuf_out, or_11_out, RC_q, rom_4_data, SP_q, subtractor_1_out, subtractor_2_out, xor_1_out;
  wire [15:4] IR_q;

  Decoder #(.select(2)) decoder_1 (
    .out0(decoder_1_out0), .out1(decoder_1_out1), .out3(decoder_1_out3), .sel({in_1, in_2}));  // open: out2, en
  Clock clock_1 (.out(clock_1_out));
  Clock #(.highDuration(5), .lowDuration(5)) clock_2 (.out(clock_2_out));
  Register #(.width(16)) IR (.D(out_34), .Q({IR_q, ALUOp}), .clk(IRClk));  // open: en, clr
  and and_1 (and_1_out, PCCondLoad, JumpAccepted);
  assign controlled_buffer_1_out = decoder_1_out0 ? clock_1_out : 1'bz;  // Controlled_Buffer controlled_buffer_1
  assign controlled_buffer_1_out = decoder_1_out1 ? clock_2_out : 1'bz;  // Controlled_Buffer controlled_buffer_2
  assign controlled_buffer_1_out = decoder_1_out3 ? in_3 : 1'bz;  // Controlled_Buffer controlled_buffer_3
  Counter #(.width(5), .max('h1f)) SeqCntr (
    .Q(SeqCntr_q), .clk(MainClock), .clr(MCRST));  // open: load, D, count, carry
  not not_1 (not_1_out, or_2_out);
  or or_1 (or_1_out, PCUp, or_2_out);
  or or_2 (or_2_out, PCLoad, and_1_out);
  Register #(.width(16)) RC (.D(out_34), .Q(RC_q), .clk(RCClk));  // open: en, clr
  Register #(.width(16)) BP (.Q(BP_q));  // open: D, en, clk, clr
  Decoder #(.select(2)) decoder_2 (
    .out0(decoder_2_out0), .out1(decoder_2_out1), .out2(decoder_2_out2), .out3(decoder_2_out3),
    .sel(counter_1_q));  // open: en
  Counter #(.width(2), .max('h3)) counter_1 (
    .Q(counter_1_q), .clk(controlled_buffer_1_out));  // open: load, D, count, carry, clr
  Register #(.width(5)) mCodeAL (.D(SeqCntr_q), .Q(mCodeAL_q), .clk(InvClock));  // open: en, clr
  Counter #(.width(14), .max('h3fff)) PC (
    .load(or_2_out), .D(out_34[15:2]), .count(not_1_out), .Q(PC_q), .clk(or_1_out));  // open: carry, clr
  assign out_34 = in_6 ? in_9 : 16'bz;  // Controlled_Buffer controlled_buffer_4
  Hex_Digit_Display hex_digit_display_1 (.value(out_34[15:12]));  // open: dp
  Hex_Digit_Display hex_digit_display_2 (.value(out_34[11:8]));  // open: dp
  Adder #(.width(16)) adder_1 (.a(RC_q), .b(BP_q), .out(adder_1_out));  // open: cin, cout
  not not_2 (not_2_out, 1'b0);
  or or_3 (MainClock, decoder_2_out0, decoder_2_out1);
  or or_4 (OverlapClock, decoder_2_out1, decoder_2_out2);
  or or_5 (InvClock, decoder_2_out2, decoder_2_out3);
  assign out_34 = PCOE ? {PC_q, 2'b00} : 16'bz;  // Controlled_Buffer PCBuf
  Hex_Digit_Display hex_digit_display_3 (.value(out_34[7:4]));  // open: dp
  Hex_Digit_Display hex_digit_display_4 (.value(out_34[3:0]));  // open: dp
  assign out_34 = RCOE ? controlled_buffer_5_out : 16'bz;  // Controlled_Buffer RCBuf
  assign controlled_buffer_5_out = not_2_out ? RC_q : 16'bz;  // Controlled_Buffer controlled_buffer_5
  assign controlled_buffer_5_out = 1'b0 ? adder_1_out : 16'bz;  // Controlled_Buffer controlled_buffer_6
  Register #(.width(14)) PCLatch (.D(out_34[15:2]), .Q(PCLatch_q), .clk(PCLatchClk));  // open: en, clr
  ROM #(.addrWidth(16)) rom_1 (.addr({IRQ, IR_q[12:4], ALUOp[3], mCodeAL_q}), .data(rom_1_data));  // open: sel
  Pull_Resistor pull_resistor_1 (.node(pull_resistor_1_node));
  assign pull_resistor_1_node = MainClock ? rom_1_data : 8'bz;  // Controlled_Buffer controlled_buffer_7
  Pull_Resistor pull_resistor_2 (.node(pull_resistor_2_node));
  assign pull_resistor_2_node = MainClock ? rom_2_data : 8'bz;  // Controlled_Buffer controlled_buffer_8
  ROM #(.addrWidth(16)) rom_2 (.addr({IRQ, IR_q[12:4], ALUOp[3], mCodeAL_q}), .data(rom_2_data));  // open: sel
  assign {AccessCode, controlled_buffer_9_out} = MainClock ? rom_3_data : 8'bz;  // Controlled_Buffer controlled_buffer_9
  ROM #(.addrWidth(16)) rom_3 (.addr({IRQ, IR_q[12:4], ALUOp[3], mCodeAL_q}), .data(rom_3_data));  // open: sel
  Pull_Resistor pull_resistor_3 (.node({AccessCode, controlled_buffer_9_out}));
  assign out_34 = PCLatchOE ? {PCLatch_q, PCV1, PCV0} : 16'bz;  // Controlled_Buffer PCBuf_2
  assign PCOE = in_5 ? in_7 : 1'bz;  // Controlled_Buffer controlled_buffer_10
  assign PCLatchOE = in_5 ? in_8 : 1'bz;  // Controlled_Buffer controlled_buffer_11
  assign MR = in_5 ? in_10 : 1'bz;  // Controlled_Buffer controlled_buffer_12
  assign ALUOE = in_5 ? in_11 : 1'bz;  // Controlled_Buffer controlled_buffer_13
  assign SPOE = in_5 ? in_12 : 1'bz;  // Controlled_Buffer controlled_buffer_14
  assign RCOE = in_5 ? in_13 : 1'bz;  // Controlled_Buffer controlled_buffer_15
  assign IRClk = in_5 ? in_14 : 1'bz;  // Controlled_Buffer controlled_buffer_16
  assign PCLoad = in_5 ? in_15 : 1'bz;  // Controlled_Buffer controlled_buffer_17
  assign PCLatchClk = in_5 ? in_16 : 1'bz;  // Controlled_Buffer controlled_buffer_18
  assign RCClk = in_5 ? in_17 : 1'bz;  // Controlled_Buffer controlled_buffer_19
  assign RAClk = in_5 ? in_18 : 1'bz;  // Controlled_Buffer controlled_buffer_20
  assign RBClk = in_5 ? in_19 : 1'bz;  // Controlled_Buffer controlled_buffer_21
  assign ML = in_5 ? in_20 : 1'bz;  // Controlled_Buffer controlled_buffer_22
  assign MWProtected = in_5 ? in_21 : 1'bz;  // Controlled_Buffer controlled_buffer_23
  assign PCCondLoad = in_5 ? in_22 : 1'bz;  // Controlled_Buffer controlled_buffer_24
  assign SPLoad = in_5 ? in_23 : 1'bz;  // Controlled_Buffer controlled_buffer_25
  assign PCUp = in_5 ? in_24 : 1'bz;  // Controlled_Buffer controlled_buffer_26
  assign PCV0 = in_5 ? in_25 : 1'bz;  // Controlled_Buffer controlled_buffer_27
  assign PCV1 = in_5 ? in_26 : 1'bz;  // Controlled_Buffer controlled_buffer_28
  assign SPUp = in_5 ? in_27 : 1'bz;  // Controlled_Buffer controlled_buffer_29
  assign SPDown = in_5 ? in_28 : 1'bz;  // Controlled_Buffer controlled_buffer_30
  assign MCRST = in_5 ? in_29 : 1'bz;  // Controlled_Buffer controlled_buffer_31
  assign UserSet = in_5 ? in_30 : 1'bz;  // Controlled_Buffer controlled_buffer_32
  assign UserReset = in_5 ? in_31 : 1'bz;  // Controlled_Buffer controlled_buffer_33
  assign controlled_buffer_34_out = in_5 ? in_32 : 1'bz;  // Controlled_Buffer controlled_buffer_34
  assign controlled_buffer_35_out = in_5 ? in_33 : 1'bz;  // Controlled_Buffer controlled_buffer_35
  not not_3 (not_3_out, UserMode_q);
  S_R_Flip_Flop #(.trigger("high")) UserMode (
    .S(UserSet), .clk(1'b1), .R(UserReset), .Q(UserMode_q));  // open: Qn, preset, reset, en
  or or_6 (or_6_out, AddrBUS[13], not_3_out, AddrBUS[15]);
  or or_7 (or_7_out, SPLoad, SPDown);
  or or_8 (or_8_out, SPUp, SPDown);
  or or_9 (or_9_out, SPLoad, SPDown, SPUp);
  Decoder #(.select(3)) decoder_3 (
    .out1(PCOE), .out2(PCLatchOE), .out3(MR), .out4(ALUOE), .out5(SPOE), .out6(RCOE), .out7(IntOE),
    .sel(pull_resistor_1_node[2:0]), .en(1'b1));  // open: out0
  assign {UserReset, UserSet, MCRST, SPDown, SPUp, PCV1, PCV0, PCUp} = 1'b1 ? {controlled_buffer_9_out[4:0], pull_resistor_2_node[7:5]} : 8'bz;  // Controlled_Buffer controlled_buffer_36
  assign {controlled_buffer_37_out, IntReset, Interrupt} = 1'b1 ? {undriven, controlled_buffer_9_out[6:5]} : 8'bz;  // Controlled_Buffer controlled_buffer_37
  and and_2 (MW, MWProtected, or_6_out);
  Register #(.width(16)) u_ML (.D(out_34), .Q(AddrBUS), .clk(ML));  // open: en, clr
  assign out_34 = SPOE ? SP_q : 16'bz;  // Controlled_Buffer SPBuff
  Counter #(.width(16), .max('hffff)) SP (
    .load(or_7_out), .D(out_34), .count(or_8_out), .Q(SP_q), .clk(or_9_out));  // open: carry, clr
  assign and_3_out = {pull_resistor_2_node[2:0], pull_resistor_1_node[7:3]} & {8{OverlapClock}};  // AND_Gate and_3, 8 bits wide
  assign {MWProtected, ML, RCClk, RBClk, RAClk, PCLatchClk, PCLoad, IRClk} = 1'b1 ? and_3_out : 8'bz;  // Controlled_Buffer controlled_buffer_38
  assign {controlled_buffer_39_out, PCCondLoad, SPLoad} = 1'b1 ? and_4_out : 8'bz;  // Controlled_Buffer controlled_buffer_39
  assign and_4_out = {undriven_2, pull_resistor_2_node[4:3]} & {8{OverlapClock}};  // AND_Gate and_4, 8 bits wide
  LED led_1 ();  // open: in
  assign controlled_buffer_40_out = decoder_4_out0 ? {1'b0, RA_q} : 16'bz;  // Controlled_Buffer controlled_buffer_40
  assign controlled_buffer_40_out = decoder_4_out1 ? {RA_q[13:0], RA_q_2[1], 1'b0} : 16'bz;  // Controlled_Buffer controlled_buffer_41
  assign controlled_buffer_40_out = decoder_4_out2 ? {{8{1'b0}}, RA_q[14:7]} : 16'bz;  // Controlled_Buffer controlled_buffer_42
  Decoder #(.select(2)) decoder_4 (
    .out0(decoder_4_out0), .out1(decoder_4_out1), .out2(decoder_4_out2), .out3(decoder_4_out3), .sel(RB_q));  // open: en
  assign controlled_buffer_40_out = decoder_4_out3 ? {RA_q[6:0], RA_q_2[1], {8{1'b0}}} : 16'bz;  // Controlled_Buffer controlled_buffer_43
  Decoder #(.select(3)) decoder_5 (
    .out0(decoder_5_out0), .out2(decoder_5_out2), .out3(decoder_5_out3), .sel(AddrBUS[15:13]));  // open: out1, out4, out5, out6, out7, en
  Register #(.width(16)) BP_2 (.D(out_34), .en(AddrBUS[13]), .Q(BP_2_q), .clk(MW));  // open: clr
  Register #(.width(16)) RA (.D(out_34), .Q({RA_q, RA_q_2[1]}), .clk(RAClk));  // open: en, clr
  Register #(.width(16)) RB (.D(out_34), .Q({RB_q_2, RB_q}), .clk(RBClk));  // open: en, clr
  or or_10 (or_10_out, decoder_5_out2, decoder_5_out3);
  Adder #(.width(16)) adder_2 (.a({RA_q, RA_q_2[1]}), .b({RB_q_2, RB_q}), .out(adder_2_out));  // open: cin, cout
  Subtractor #(.width(16)) subtractor_1 (
    .a({RA_q, RA_q_2[1]}), .b({RB_q_2, RB_q}), .out(subtractor_1_out));  // open: bin, bout
  assign and_5_out = {RA_q, RA_q_2[1]} & {RB_q_2, RB_q};  // AND_Gate and_5, 16 bits wide
  assign or_11_out = {RA_q, RA_q_2[1]} | {RB_q_2, RB_q};  // OR_Gate or_11, 16 bits wide
  assign xor_1_out = {RA_q, RA_q_2[1]} ^ {RB_q_2, RB_q};  // XOR_Gate xor_1, 16 bits wide
  Comparator #(.width(16)) comparator_1 (
    .a({RA_q, RA_q_2[1]}), .b({RB_q_2, RB_q}), .gt(comparator_1_gt[0]), .eq(comparator_1_gt[1]),
    .lt(comparator_1_gt[2]));
  Adder #(.width(16)) adder_3 (.a({4'b0000, AddrBUS[11:0]}), .b(BP_2_q), .out(adder_3_out));  // open: cin, cout
  Subtractor #(.width(16)) subtractor_2 (
    .a(BP_2_q), .b({4'b0000, AddrBUS[11:0]}), .out(subtractor_2_out));  // open: bin, bout
  assign out_34 = ALUOE ? MainBuf_out : 16'bz;  // Controlled_Buffer controlled_buffer_44
  assign and_6_out = comparator_1_gt & ALUOp[2:0];  // AND_Gate and_6, 3 bits wide
  or or_12 (JumpAccepted, and_6_out[2], and_6_out[1], and_6_out[0]);
  assign buffer_1_out = out_34;  // Buffer buffer_1, 16 bits wide
  assign out_34 = MR ? buffer_1_out : 16'bz;  // Controlled_Buffer controlled_buffer_45
  RAM #(.addrWidth(14), .dataWidth(16)) ram_1 (
    .addr(AddrBUS[13:0]), .data(buffer_1_out), .sel(or_10_out), .clk(MW), .ld(MR));  // open: clr
  ROM #(.addrWidth(13), .dataWidth(16)) rom_4 (.addr(AddrBUS[12:0]), .data(rom_4_data), .sel(decoder_5_out0));
  assign out_34 = MR ? rom_4_data : 16'bz;  // Controlled_Buffer controlled_buffer_46
  assign controlled_buffer_47_out = not_4_out ? adder_3_out : 16'bz;  // Controlled_Buffer controlled_buffer_47
  not not_4 (not_4_out, AddrBUS[12]);
  assign controlled_buffer_47_out = AddrBUS[12] ? subtractor_2_out : 16'bz;  // Controlled_Buffer controlled_buffer_48
  and and_7 (and_7_out, AddrBUS[13], MR);
  assign controlled_buffer_49_out = decoder_6_out0 ? adder_2_out : 16'bz;  // Controlled_Buffer controlled_buffer_49
  assign controlled_buffer_49_out = decoder_6_out1 ? subtractor_1_out : 16'bz;  // Controlled_Buffer controlled_buffer_50
  assign controlled_buffer_49_out = decoder_6_out2 ? and_5_out : 16'bz;  // Controlled_Buffer controlled_buffer_51
  Decoder #(.select(3)) decoder_6 (
    .out0(decoder_6_out0), .out1(decoder_6_out1), .out2(decoder_6_out2), .out3(decoder_6_out3),
    .out4(decoder_6_out4), .out5(decoder_6_out5), .sel(ALUOp[2:0]));  // open: out6, out7, en
  assign out_34 = and_7_out ? controlled_buffer_47_out : 16'bz;  // Controlled_Buffer controlled_buffer_52
  assign MainBuf_out = not_5_out ? controlled_buffer_49_out : 16'bz;  // Controlled_Buffer MainBuf
  not not_5 (not_5_out, decoder_6_out5);
  assign controlled_buffer_49_out = decoder_6_out3 ? or_11_out : 16'bz;  // Controlled_Buffer controlled_buffer_53
  assign controlled_buffer_49_out = decoder_6_out4 ? xor_1_out : 16'bz;  // Controlled_Buffer controlled_buffer_54
  assign MainBuf_out = decoder_6_out5 ? controlled_buffer_40_out : 16'bz;  // Controlled_Buffer ShiftBuf

  // Other names for the same wires on the sheet: BUS[15:0] = out_34

  // Notes on the sheet:
  //   contents of rom_1 (hex, n*v repeats v):
  //   21 b 2 43 2 83 2 3 6 4 22*0 21 b 2 43 2 83 2 3 6 23*0 21 b 2 3 6 43 2 83 2 3 6 4 20*0 21 b 2 3 6 43
  //   2 83 2 3 6 21*0 21 b 2 3 6 3 6 43 2 83 2 3 6 4 18*0 21 b 2 3 6 3 6 43 2 83 2 3 6 19*0 21 b 2 3 6 3 6
  //   3 6 43 2 83 2 3 6 4 16*0 21 b 2 3 6 3 6 3 6 43 2 83 2 3 6 17*0 21 b 2 83 2 3 6 4 24*0 21 b 2 83 2 3
  //   6 25*0 21 b 41 2 83 2 3 6 4 23*0 21 b 41 2 83 2 3 6 24*0 21 b 45 2 83 2 3 6 4 23*0 21 b 45 2 83 2 3
  //   6 24*0 21 b 2 83 2 3 6 4 24*0 21 b 2 83 2 3 6 25*0 21 b 2 43 2 3 6 83 2 3 6 4 20*0 21 b 2 43 2 3 6
  //   83 2 3 6 21*0 21 b 2 3 6 43 2 3 6 83 2 3 6 4 18*0 21 b 2 3 6 43 2 3 6 83 2 3 6 19*0 21 b 2 3 6 3 6
  //   43 2 3 6 83 2 3 6 4 16*0 21 b 2 3 6 3 6 43 2 3 6 83 2 3 6 17*0 21 b 2 3 6 3 6 3 6 43 2 3 6 83 2 3 6
  //   4 14*0 21 b 2 3 6 3 6 3 6 43 2 3 6 83 2 3 6 15*0 21 b 2 3 6 83 2 3 6 4 22*0 21 b 2 3 6 83 2 3 6 23*0
  //   21 b 41 2 3 6 83 2 3 6 4 21*0 21 b 41 2 3 6 83 2 3 6 22*0 21 b 45 2 3 6 83 2 3 6 4 21*0 21 b 45 2 3
  //   6 83 2 3 6 22*0 21 b 2 3 6 83 2 3 6 4 22*0 21 b 2 3 6 83 2 3 6 23*0 21 b 2 43 2 3 6 3 6 83 2 3 6 4
  //   18*0 21 b 2 43 2 3 6 3 6 83 2 3 6 19*0 21 b 2 3 6 43 2 3 6 3 6 83 2 3 6 4 16*0 21 b 2 3 6 43 2 3 6 3
  //   6 83 2 3 6 17*0 21 b 2 3 6 3 6 43 2 3 6 3 6 83 2 3 6 4 14*0 21 b 2 3 6 3 6 43 2 3 6 3 6 83 2 3 6
  //   15*0 21 b 2 3 6 3 6 3 6 43 2 3 6 3 6 83 2 3 6 4 12*0 21 b 2 3 6 3 6 3 6 43 2 3 6 3 6 83 2 3 6 13*0
  //   21 b 2 3 6 3 6 83 2 3 6 4 20*0 21 b 2 3 6 3 6 83 2 3 6 21*0 21 b 41 2 3 6 3 6 83 2 3 6 4 19*0 21 b
  //   41 2 3 6 3 6 83 2 3 6 20*0 21 b 45 2 3 6 3 6 83 2 3 6 4 19*0 21 b 45 2 3 6 3 6 83 2 3 6 20*0 21 b 2
  //   3 6 3 6 83 2 3 6 4 20*0 21 b 2 3 6 3 6 83 2 3 6 21*0 21 b 2 43 2 3 6 3 6 3 6 83 2 3 6 4 16*0 21 b 2
  //   43 2 3 6 3 6 3 6 83 2 3 6 17*0 21 b 2 3 6 43 2 3 6 3 6 3 6 83 2 3 6 4 14*0 21 b 2 3 6 43 2 3 6 3 6 3
  //   6 83 2 3 6 15*0 21 b 2 3 6 3 6 43 2 3 6 3 6 3 6 83 2 3 6 4 12*0 21 b 2 3 6 3 6 43 2 3 6 3 6 3 6 83 2
  //   3 6 13*0 21 b 2 3 6 3 6 3 6 43 2 3 6 3 6 3 6 83 2 3 6 4 10*0 21 b 2 3 6 3 6 3 6 43 2 3 6 3 6 3 6 83
  //   2 3 6 11*0 21 b 2 3 6 3 6 3 6 83 2 3 6 4 18*0 21 b 2 3 6 3 6 3 6 83 2 3 6 19*0 21 b 41 2 3 6 3 6 3 6
  //   83 2 3 6 4 17*0 21 b 41 2 3 6 3 6 3 6 83 2 3 6 18*0 21 b 45 2 3 6 3 6 3 6 83 2 3 6 4 17*0 21 b 45 2
  //   3 6 3 6 3 6 83 2 3 6 18*0 21 b 2 3 6 3 6 3 6 83 2 3 6 4 18*0 21 b 2 3 6 3 6 3 6 83 2 3 6 19*0 21 b 2
  //   43 2 83 2 3 6 3 6 4 20*0 21 b 2 43 2 83 2 3 6 3 6 21*0 21 b 2 3 6 43 2 83 2 3 6 3 6 4 18*0 21 b 2 3
  //   6 43 2 83 2 3 6 3 6 19*0 21 b 2 3 6 3 6 43 2 83 2 3 6 3 6 4 16*0 21 b 2 3 6 3 6 43 2 83 2 3 6 3 6
  //   17*0 21 b 2 3 6 3 6 3 6 43 2 83 2 3 6 3 6 4 14*0 21 b 2 3 6 3 6 3 6 43 2 83 2 3 6 3 6 15*0 21 b 2 83
  //   2 3 6 3 6 4 22*0 21 b 2 83 2 3 6 3 6 23*0 21 b 41 2 83 2 3 6 3 6 4 21*0 21 b 41 2 83 2 3 6 3 6 22*0
  //   21 b 45 2 83 2 3 6 3 6 4 21*0 21 b 45 2 83 2 3 6 3 6 22*0 21 b 2 83 2 3 6 3 6 4 22*0 21 b 2 83 2 3 6
  //   3 6 23*0 21 b 2 43 2 3 6 83 2 3 6 3 6 4 18*0 21 b 2 43 2 3 6 83 2 3 6 3 6 19*0 21 b 2 3 6 43 2 3 6
  //   83 2 3 6 3 6 4 16*0 21 b 2 3 6 43 2 3 6 83 2 3 6 3 6 17*0 21 b 2 3 6 3 6 43 2 3 6 83 2 3 6 3 6 4
  //   14*0 21 b 2 3 6 3 6 43 2 3 6 83 2 3 6 3 6 15*0 21 b 2 3 6 3 6 3 6 43 2 3 6 83 2 3 6 3 6 4 12*0 21 b
  //   2 3 6 3 6 3 6 43 2 3 6 83 2 3 6 3 6 13*0 21 b 2 3 6 83 2 3 6 3 6 4 20*0 21 b 2 3 6 83 2 3 6 3 6 21*0
  //   21 b 41 2 3 6 83 2 3 6 3 6 4 19*0 21 b 41 2 3 6 83 2 3 6 3 6 20*0 21 b 45 2 3 6 83 2 3 6 3 6 4 19*0
  //   21 b 45 2 3 6 83 2 3 6 3 6 20*0 21 b 2 3 6 83 2 3 6 3 6 4 20*0 21 b 2 3 6 83 2 3 6 3 6 21*0 21 b 2
  //   43 2 3 6 3 6 83 2 3 6 3 6 4 16*0 21 b 2 43 2 3 6 3 6 83 2 3 6 3 6 17*0 21 b 2 3 6 43 2 3 6 3 6 83 2
  //   3 6 3 6 4 14*0 21 b 2 3 6 43 2 3 6 3 6 83 2 3 6 3 6 15*0 21 b 2 3 6 3 6 43 2 3 6 3 6 83 2 3 6 3 6 4
  //   12*0 21 b 2 3 6 3 6 43 2 3 6 3 6 83 2 3 6 3 6 13*0 21 b 2 3 6 3 6 3 6 43 2 3 6 3 6 83 2 3 6 3 6 4
  //   10*0 21 b 2 3 6 3 6 3 6 43 2 3 6 3 6 83 2 3 6 3 6 11*0 21 b 2 3 6 3 6 83 2 3 6 3 6 4 18*0 21 b 2 3 6
  //   3 6 83 2 3 6 3 6 19*0 21 b 41 2 3 6 3 6 83 2 3 6 3 6 4 17*0 21 b 41 2 3 6 3 6 83 2 3 6 3 6 18*0 21 b
  //   45 2 3 6 3 6 83 2 3 6 3 6 4 17*0 21 b 45 2 3 6 3 6 83 2 3 6 3 6 18*0 21 b 2 3 6 3 6 83 2 3 6 3 6 4
  //   18*0 21 b 2 3 6 3 6 83 2 3 6 3 6 19*0 21 b 2 43 2 3 6 3 6 3 6 83 2 3 6 3 6 4 14*0 21 b 2 43 2 3 6 3
  //   6 3 6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
  //   contents of rom_2 (hex, n*v repeats v):
  //   2 20 42 0 82 0 c2 1 2 4 22*0 2 20 42 0 82 0 c2 1 10 23*0 2 20 42 1 2 0 82 0 c2 1 2 4 20*0 2 20 42 1
  //   2 0 82 0 c2 1 10 21*0 2 20 42 1 2 1 2 0 82 0 c2 1 2 4 18*0 2 20 42 1 2 1 2 0 82 0 c2 1 10 19*0 2 20
  //   42 1 2 1 2 1 2 0 82 0 c2 1 2 4 16*0 2 20 42 1 2 1 2 1 2 0 82 0 c2 1 10 17*0 2 20 82 0 c2 1 2 4 24*0
  //   2 20 82 0 c2 1 10 25*0 2 20 0 82 0 c2 1 2 4 23*0 2 20 0 82 0 c2 1 10 24*0 2 20 0 82 0 c2 1 2 4 23*0
  //   2 20 0 82 0 c2 1 10 24*0 2 20 82 0 c2 1 2 4 24*0 2 20 82 0 c2 1 10 25*0 2 20 42 0 82 1 2 0 c2 1 2 4
  //   20*0 2 20 42 0 82 1 2 0 c2 1 10 21*0 2 20 42 1 2 0 82 1 2 0 c2 1 2 4 18*0 2 20 42 1 2 0 82 1 2 0 c2
  //   1 10 19*0 2 20 42 1 2 1 2 0 82 1 2 0 c2 1 2 4 16*0 2 20 42 1 2 1 2 0 82 1 2 0 c2 1 10 17*0 2 20 42 1
  //   2 1 2 1 2 0 82 1 2 0 c2 1 2 4 14*0 2 20 42 1 2 1 2 1 2 0 82 1 2 0 c2 1 10 15*0 2 20 82 1 2 0 c2 1 2
  //   4 22*0 2 20 82 1 2 0 c2 1 10 23*0 2 20 0 82 1 2 0 c2 1 2 4 21*0 2 20 0 82 1 2 0 c2 1 10 22*0 2 20 0
  //   82 1 2 0 c2 1 2 4 21*0 2 20 0 82 1 2 0 c2 1 10 22*0 2 20 82 1 2 0 c2 1 2 4 22*0 2 20 82 1 2 0 c2 1
  //   10 23*0 2 20 42 0 82 1 2 1 2 0 c2 1 2 4 18*0 2 20 42 0 82 1 2 1 2 0 c2 1 10 19*0 2 20 42 1 2 0 82 1
  //   2 1 2 0 c2 1 2 4 16*0 2 20 42 1 2 0 82 1 2 1 2 0 c2 1 10 17*0 2 20 42 1 2 1 2 0 82 1 2 1 2 0 c2 1 2
  //   4 14*0 2 20 42 1 2 1 2 0 82 1 2 1 2 0 c2 1 10 15*0 2 20 42 1 2 1 2 1 2 0 82 1 2 1 2 0 c2 1 2 4 12*0
  //   2 20 42 1 2 1 2 1 2 0 82 1 2 1 2 0 c2 1 10 13*0 2 20 82 1 2 1 2 0 c2 1 2 4 20*0 2 20 82 1 2 1 2 0 c2
  //   1 10 21*0 2 20 0 82 1 2 1 2 0 c2 1 2 4 19*0 2 20 0 82 1 2 1 2 0 c2 1 10 20*0 2 20 0 82 1 2 1 2 0 c2
  //   1 2 4 19*0 2 20 0 82 1 2 1 2 0 c2 1 10 20*0 2 20 82 1 2 1 2 0 c2 1 2 4 20*0 2 20 82 1 2 1 2 0 c2 1
  //   10 21*0 2 20 42 0 82 1 2 1 2 1 2 0 c2 1 2 4 16*0 2 20 42 0 82 1 2 1 2 1 2 0 c2 1 10 17*0 2 20 42 1 2
  //   0 82 1 2 1 2 1 2 0 c2 1 2 4 14*0 2 20 42 1 2 0 82 1 2 1 2 1 2 0 c2 1 10 15*0 2 20 42 1 2 1 2 0 82 1
  //   2 1 2 1 2 0 c2 1 2 4 12*0 2 20 42 1 2 1 2 0 82 1 2 1 2 1 2 0 c2 1 10 13*0 2 20 42 1 2 1 2 1 2 0 82 1
  //   2 1 2 1 2 0 c2 1 2 4 10*0 2 20 42 1 2 1 2 1 2 0 82 1 2 1 2 1 2 0 c2 1 10 11*0 2 20 82 1 2 1 2 1 2 0
  //   c2 1 2 4 18*0 2 20 82 1 2 1 2 1 2 0 c2 1 10 19*0 2 20 0 82 1 2 1 2 1 2 0 c2 1 2 4 17*0 2 20 0 82 1 2
  //   1 2 1 2 0 c2 1 10 18*0 2 20 0 82 1 2 1 2 1 2 0 c2 1 2 4 17*0 2 20 0 82 1 2 1 2 1 2 0 c2 1 10 18*0 2
  //   20 82 1 2 1 2 1 2 0 c2 1 2 4 18*0 2 20 82 1 2 1 2 1 2 0 c2 1 10 19*0 2 20 42 0 82 0 c2 1 2 1 2 4
  //   20*0 2 20 42 0 82 0 c2 1 2 1 10 21*0 2 20 42 1 2 0 82 0 c2 1 2 1 2 4 18*0 2 20 42 1 2 0 82 0 c2 1 2
  //   1 10 19*0 2 20 42 1 2 1 2 0 82 0 c2 1 2 1 2 4 16*0 2 20 42 1 2 1 2 0 82 0 c2 1 2 1 10 17*0 2 20 42 1
  //   2 1 2 1 2 0 82 0 c2 1 2 1 2 4 14*0 2 20 42 1 2 1 2 1 2 0 82 0 c2 1 2 1 10 15*0 2 20 82 0 c2 1 2 1 2
  //   4 22*0 2 20 82 0 c2 1 2 1 10 23*0 2 20 0 82 0 c2 1 2 1 2 4 21*0 2 20 0 82 0 c2 1 2 1 10 22*0 2 20 0
  //   82 0 c2 1 2 1 2 4 21*0 2 20 0 82 0 c2 1 2 1 10 22*0 2 20 82 0 c2 1 2 1 2 4 22*0 2 20 82 0 c2 1 2 1
  //   10 23*0 2 20 42 0 82 1 2 0 c2 1 2 1 2 4 18*0 2 20 42 0 82 1 2 0 c2 1 2 1 10 19*0 2 20 42 1 2 0 82 1
  //   2 0 c2 1 2 1 2 4 16*0 2 20 42 1 2 0 82 1 2 0 c2 1 2 1 10 17*0 2 20 42 1 2 1 2 0 82 1 2 0 c2 1 2 1 2
  //   4 14*0 2 20 42 1 2 1 2 0 82 1 2 0 c2 1 2 1 10 15*0 2 20 42 1 2 1 2 1 2 0 82 1 2 0 c2 1 2 1 2 4 12*0
  //   2 20 42 1 2 1 2 1 2 0 82 1 2 0 c2 1 2 1 10 13*0 2 20 82 1 2 0 c2 1 2 1 2 4 20*0 2 20 82 1 2 0 c2 1 2
  //   1 10 21*0 2 20 0 82 1 2 0 c2 1 2 1 2 4 19*0 2 20 0 82 1 2 0 c2 1 2 1 10 20*0 2 20 0 82 1 2 0 c2 1 2
  //   1 2 4 19*0 2 20 0 82 1 2 0 c2 1 2 1 10 20*0 2 20 82 1 2 0 c2 1 2 1 2 4 20*0 2 20 82 1 2 0 c2 1 2 1
  //   10 21*0 2 20 42 0 82 1 2 1 2 0 c2 1 2 1 2 4 16*0 2 20 42 0 82 1 2 1 2 0 c2 1 2 1 10 17*0 2 20 42 1 2
  //   0 82 1 2 1 2 0 c2 1 2 1 2 4 14*0 2 20 42 1 2 0 82 1 2 1 2 0 c2 1 2 1 10 15*0 2 20 42 1 2 1 2 0 82 1
  //   2 1 2 0 c2 1 2 1 2 4 12*0 2 20 42 1 2 1 2 0 82 1 2 1 2 0 c2 1 2 1 10 13*0 2 20 42 1 2 1 2 1 2 0 82 1
  //   2 1 2 0 c2 1 2 1 2 4 10*0 2 20 42 1 2 1 2 1 2 0 82 1 2 1 2 0 c2 1 2 1 10 11*0 2 20 82 1 2 1 2 0 c2 1
  //   2 1 2 4 18*0 2 20 82 1 2 1 2 0 c2 1 2 1 10 19*0 2 20 0 82 1 2 1 2 0 c2 1 2 1 2 4 17*0 2 20 0 82 1 2
  //   1 2 0 c2 1 2 1 10 18*0 2 20 0 82 1 2 1 2 0 c2 1 2 1 2 4 17*0 2 20 0 82 1 2 1 2 0 c2 1 2 1 10 18*0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
  //   contents of rom_3 (hex, n*v repeats v):
  //   10*0 4 30*0 4 34*0 4 30*0 4 34*0 4 30*0 4 34*0 4 30*0 4 24*0 4 30*0 4 33*0 4 30*0 4 32*0 4 30*0 4
  //   31*0 4 30*0 4 36*0 4 30*0 4 34*0 4 30*0 4 34*0 4 30*0 4 34*0 4 30*0 4 24*0 4 30*0 4 33*0 4 30*0 4
  //   32*0 4 30*0 4 31*0 4 30*0 4 36*0 4 30*0 4 34*0 4 30*0 4 34*0 4 30*0 4 34*0 4 30*0 4 24*0 4 30*0 4
  //   33*0 4 30*0 4 32*0 4 30*0 4 31*0 4 30*0 4 36*0 4 30*0 4 34*0 4 30*0 4 34*0 4 30*0 4 34*0 4 30*0 4
  //   24*0 4 30*0 4 33*0 4 30*0 4 32*0 4 30*0 4 31*0 4 30*0 4 30*0 4 30*0 4 34*0 4 30*0 4 34*0 4 30*0 4
  //   34*0 4 30*0 4 24*0 4 30*0 4 33*0 4 30*0 4 32*0 4 30*0 4 31*0 4 30*0 4 36*0 4 30*0 4 34*0 4 30*0 4
  //   34*0 4 30*0 4 34*0 4 30*0 4 24*0 4 30*0 4 33*0 4 30*0 4 32*0 4 30*0 4 31*0 4 30*0 4 36*0 4 30*0 4
  //   34*0 4 30*0 4 34*0 4 30*0 4 34*0 4 30*0 4 24*0 4 30*0 4 33*0 4 30*0 4 32*0 4 30*0 4 31*0 4 30*0 4
  //   36*0 4 30*0 4 34*0 4 30*0 4 34*0 4 30*0 4 34*0 4 30*0 4 24*0 4 30*0 4 33*0 4 30*0 4 32*0 4 30*0 4
  //   31*0 4 30*0 4 30*0 4 30*0 4 34*0 4 30*0 4 34*0 4 30*0 4 34*0 4 30*0 4 24*0 4 30*0 4 33*0 4 30*0 4
  //   32*0 4 30*0 4 31*0 4 30*0 4 36*0 4 30*0 4 34*0 4 30*0 4 34*0 4 30*0 4 34*0 4 30*0 4 24*0 4 30*0 4
  //   33*0 4 30*0 4 32*0 4 30*0 4 31*0 4 30*0 4 36*0 4 30*0 4 34*0 4 30*0 4 34*0 4 30*0 4 34*0 4 30*0 4
  //   24*0 4 30*0 4 33*0 4 30*0 4 32*0 4 30*0 4 31*0 4 30*0 4 36*0 4 30*0 4 34*0 4 30*0 4 34*0 4 30*0 4
  //   34*0 4 30*0 4 24*0 4 30*0 4 33*0 4 30*0 4 32*0 4 30*0 4 31*0 4 30*0 4 30*0 4 30*0 4 34*0 4 30*0 4
  //   34*0 4 30*0 4 34*0 4 30*0 4 24*0 4 30*0 4 33*0 4 30*0 4 32*0 4 30*0 4 31*0 4 30*0 4 36*0 4 30*0 4
  //   34*0 4 30*0 4 34*0 4 30*0 4 34*0 4 30*0 4 24*0 4 30*0 4 33*0 4 30*0 4 32*0 4 30*0 4 31*0 4 30*0 4
  //   36*0 4 30*0 4 34*0 4 30*0 4 34*0 4 30*0 4 34*0 4 30*0 4 24*0 4 30*0 4 33*0 4 30*0 4 32*0 4 30*0 4
  //   31*0 4 30*0 4 36*0 4 30*0 4 34*0 4 30*0 4 34*0 4 30*0 4 34*0 4 30*0 4 24*0 4 30*0 4 33*0 4 30*0 4
  //   32*0 4 30*0 4 31*0 4 30*0 4 19*0 4 31*0 4 33*0 4 31*0 4 33*0 4 31*0 4 33*0 4 31*0 4 23*0 4 31*0 4
  //   32*0 4 31*0 4 31*0 4 31*0 4 30*0 4 31*0 4 35*0 4 31*0 4 33*0 4 31*0 4 33*0 4 31*0 4 33*0 4 31*0 4
  //   23*0 4 31*0 4 32*0 4 31*0 4 31*0 4 31*0 4 30*0 4 31*0 4 35*0 4 31*0 4 33*0 4 31*0 4 33*0 4 31*0 4
  //   33*0 4 31*0 4 23*0 4 31*0 4 32*0 4 31*0 4 31*0 4 31*0 4 30*0 4 31*0 4 35*0 4 31*0 4 33*0 4 31*0 4
  //   33*0 4 31*0 4 33*0 4 31*0 4 23*0 4 31*0 4 32*0 4 31*0 4 31*0 4 31*0 4 30*0 4 31*0 4 27*0 4 31*0 4
  //   33*0 4 31*0 4 33*0 4 31*0 4 33*0 4 31*0 4 23*0 4 31*0 4 32*0 4 31*0 4 31*0 4 31*0 4 30*0 4 31*0 4
  //   35*0 4 31*0 4 33*0 4 31*0 4 33*0 4 31*0 4 33*0 4 31*0 4 23*0 4 31*0 4 32*0 4 31*0 4 31*0 4 31*0 4
  //   30*0 4 31*0 4 35*0 4 31*0 4 33*0 4 31*0 4 33*0 4 31*0 4 33*0 4 31*0 4 23*0 4 31*0 4 32*0 4 31*0 4
  //   31*0 4 31*0 4 30*0 4 31*0 4 35*0 4 31*0 4 33*0 4 31*0 4 33*0 4 31*0 4 33*0 4 31*0 4 23*0 4 31*0 4
  //   32*0 4 31*0 4 31*0 4 31*0 4 30*0 4 31*0 4 27*0 4 31*0 4 33*0 4 31*0 4 33*0 4 31*0 4 33*0 4 31*0 4
  //   23*0 4 31*0 4 32*0 4 31*0 4 31*0 4 31*0 4 30*0 4 31*0 4 35*0 4 31*0 4 33*0 4 31*0 4 33*0 4 31*0 4
  //   33*0 4 31*0 4 23*0 4 31*0 4 32*0 4 31*0 4 31*0 4 31*0 4 30*0 4 31*0 4 35*0 4 31*0 4 33*0 4 31*0 4
  //   33*0 4 31*0 4 33*0 4 31*0 4 23*0 4 31*0 4 32*0 4 31*0 4 31*0 4 31*0 4 30*0 4 31*0 4 35*0 4 31*0 4
  //   33*0 4 31*0 4 33*0 4 31*0 4 33*0 4 31*0 4 23*0 4 31*0 4 32*0 4 31*0 4 31*0 4 31*0 4 30*0 4 31*0 4
  //   27*0 4 31*0 4 33*0 4 31*0 4 33*0 4 31*0 4 33*0 4 31*0 4 23*0 4 31*0 4 32*0 4 31*0 4 31*0 4 31*0 4
  //   30*0 4 31*0 4 35*0 4 31*0 4 33*0 4 31*0 4 33*0 4 31*0 4 33*0 4 31*0 4 23*0 4 31*0 4 32*0 4 31*0 4
  //   31*0 4 31*0 4 30*0 4 31*0 4 35*0 4 31*0 4 33*0 4 31*0 4 33*0 4 31*0 4 33*0 4 31*0 4 23*0 4 31*0 4
  //   32*0 4 31*0 4 31*0 4 31*0 4 30*0 4 31*0 4 35*0 4 31*0 4 33*0 4 31*0 4 33*0 4 31*0 4 33*0 4 31*0 4
  //   23*0 4 31*0 4 32*0 4 31*0 4 31*0 4 31*0 4 30*0 4 31*0 4 22*0 4 31*0 4 31*0 4 31*0 4 31*0 4 31*0 4
  //   31*0 4 31*0 4 31*0 4 31*0 4 31*0 4 31*0 4 31*0 4 31*0 4 31*0 4 31*0 4 35*0 2 4 30*0 2 4 32*0 2 4
  //   30*0 2 4 32*0 2 4 30*0 2 4 32*0 2 4 30*0 2 4 22*0 2 4 30*0 2 4 31*0 2 4 30*0 2 4 30*0 2 4 30*0 2 4
  //   29*0 2 4 30*0 2 4 28*0 1 8*0 4 22*0 1 8*0 4 22*0 1 10*0 4 20*0 1 10*0 4 20*0 1 12*0 4 18*0 1 12*0 4
  //   18*0 1 14*0 4 16*0 1 14*0 4 16*0 1 4*0 4 26*0 1 4*0 4 26*0 1 5*0 4 25*0 1 5*0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
  //   contents of rom_4 (hex, n*v repeats v):
  //   c00 4100 0 0 f 0 0 8 1080 15 0 0 1180 18 0 0 0 20 0 4002 f 0 0 14 1090 2000 0 0 60 0 1 2000 1080 10
  //   0 0 220 3001 1 3001 20 3001 0 4000 120 2002 3001 4001 c11 2000 1 0 1100 2000 0 0 1200
endmodule
